// Logisim project CPU_beta_v0.1.circ as structural Verilog
module main (
  output out_1,
  output out_2,
  output out_3
);

  wire CLK_out, clock_1_out, clock_2_out, clock_3_out, clock_4_out, uc_1_a_read, uc_1_a_write, uc_1_b_read,
       uc_1_b_write, uc_1_c_read, uc_1_c_write, uc_1_write_enable;
  wire [2:0] uc_1_op_codealu;
  wire [3:0] uc_1_ram_imput_address;
  wire [7:0] alu_e_1_y, ram_1_dout, registro8bits_1_out_8, registro8bits_2_out_8, registro8bits_3_out_8,
       uc_1_input_a, uc_1_input_alu_a, uc_1_input_alu_b, uc_1_input_b, uc_1_input_c, uc_1_out_8,
       uc_1_ram_imput_data;

  ALU_E alu_e_1 (
    .A(uc_1_input_alu_a), .B(uc_1_input_alu_b), .OPCODE(uc_1_op_codealu), .Y(alu_e_1_y), .Overflow(out_1),
    .Zero(out_2), .Negative(out_3));
  Clock clock_1 (.out(clock_1_out));
  registro8bits registro8bits_1 (
    .IN_8(uc_1_input_a), .CLK(clock_1_out), .Write_Enable(uc_1_a_write), .READ_ENABLE(uc_1_a_read),
    .OUT_8(registro8bits_1_out_8));  // open: R
  Clock clock_2 (.out(clock_2_out));
  Clock CLK (.out(CLK_out));
  registro8bits registro8bits_2 (
    .IN_8(uc_1_input_b), .CLK(clock_2_out), .Write_Enable(uc_1_b_write), .READ_ENABLE(uc_1_b_read),
    .OUT_8(registro8bits_2_out_8));  // open: R
  Clock clock_3 (.out(clock_3_out));
  UC uc_1 (
    .OUTPUT_C(registro8bits_3_out_8), .ALU_OUTPUT(alu_e_1_y), .OUTPUT_A(registro8bits_1_out_8),
    .OUTPUT_B(registro8bits_2_out_8), .RAM_OUTPUT(ram_1_dout), .INPUT_B(uc_1_input_b),
    .INPUT_A(uc_1_input_a), .RAM_IMPUT_DATA(uc_1_ram_imput_data), .out_8(uc_1_out_8),
    .out_20(uc_1_out_8[3:0]), .RAM_IMPUT_ADDRESS(uc_1_ram_imput_address), .A_write(uc_1_a_write),
    .B_write(uc_1_b_write), .C_Write(uc_1_c_write), .OP_CODEALU(uc_1_op_codealu), .C_READ(uc_1_c_read),
    .A_READ(uc_1_a_read), .B_READ(uc_1_b_read), .WRITE_ENABLE(uc_1_write_enable), .INPUT_C(uc_1_input_c),
    .INPUT_ALU_A(uc_1_input_alu_a), .INPUT_ALU_B(uc_1_input_alu_b));
  RAM #(.addrWidth(4), .enables("line"), .trigger("high")) ram_1 (
    .addr(uc_1_ram_imput_address), .we(uc_1_write_enable), .clk(clock_4_out), .din(uc_1_ram_imput_data),
    .dout(ram_1_dout));
  Clock clock_4 (.out(clock_4_out));
  registro8bits registro8bits_3 (
    .IN_8(uc_1_input_c), .CLK(clock_3_out), .Write_Enable(uc_1_c_write), .READ_ENABLE(uc_1_c_read),
    .OUT_8(registro8bits_3_out_8));  // open: R
  // Pins of 4 and 8 bits meet at uc_1_out_8
endmodule

module UC (
  input  [7:0] RAM_OUTPUT,
  input  [7:0] ALU_OUTPUT,
  input  [7:0] OUTPUT_A,
  input  [7:0] OUTPUT_B,
  input  [7:0] OUTPUT_C,
  output [7:0] INPUT_B,
  output [7:0] INPUT_A,
  output [7:0] out_8,
  output [7:0] INPUT_C,
  output [7:0] INPUT_ALU_A,
  output [7:0] INPUT_ALU_B,
  output A_write,
  output B_write,
  output [7:0] RAM_IMPUT_DATA,
  output C_Write,
  output C_READ,
  output A_READ,
  output B_READ,
  output [2:0] OP_CODEALU,
  output [3:0] out_20,
  output WRITE_ENABLE,
  output [3:0] RAM_IMPUT_ADDRESS
);

  wire cl, clock_1_out, clock_2_out, clock_3_out, controlunit_1_halt_enable, controlunit_1_jump_enable,
       not_1_out, not_2_out, not_3_out;
  wire [7:0] demultiplexer_1_out0;

  Demultiplexer #(.width(8)) demultiplexer_1 (.out0(demultiplexer_1_out0), .out1(INPUT_A), .in(RAM_OUTPUT), .sel(cl));
  Clock clock_1 (.out(clock_1_out));
  not not_1 (not_1_out, cl);
  not not_2 (not_2_out, cl);
  assign cl = not_3_out ? clock_1_out : 1'bz;  // Controlled_Buffer controlled_buffer_1
  not not_3 (not_3_out, controlunit_1_halt_enable);
  registro8bits registro8bits_1 (
    .IN_8(demultiplexer_1_out0), .CLK(not_1_out), .Write_Enable(not_2_out), .READ_ENABLE(cl), .OUT_8(out_8));  // open: R
  COUNTER_JUMP counter_jump_1 (.clock(cl), .JUMP(controlunit_1_jump_enable), .IN_4(out_8[3:0]), .COUNT_OUT(out_20));
  Multiplexer #(.width(4)) multiplexer_1 (.in0(out_20), .in1(out_8[3:0]), .out(RAM_IMPUT_ADDRESS), .sel(cl));
  Clock clock_2 (.out(clock_2_out));
  ControlUnit controlunit_1 (
    .CLK(clock_2_out), .OPCODE(out_8[7:4]), .A_WRITE_ENABLE(A_write), .B_WRITE_ENABLE(B_write),
    .C_WRITE_ENABLE(C_Write), .HALT_ENABLE(controlunit_1_halt_enable),
    .JUMP_ENABLE(controlunit_1_jump_enable), .ALU_OPCODE(OP_CODEALU));  // open: C_IN, C_READ_ENABLE, C_OUT, A_READ, B_READ
  Clock clock_3 (.out(clock_3_out));
  ram_enabler ram_enabler_1 (.clk(clock_3_out), .opcode(out_8[7:4]), .salida(WRITE_ENABLE));

  assign A_READ = 1'b1;
  assign B_READ = 1'b1;
  assign C_READ = 1'b1;
  assign INPUT_ALU_A = OUTPUT_A;
  assign INPUT_ALU_B = OUTPUT_B;
  assign INPUT_B = INPUT_A;
  assign INPUT_C = ALU_OUTPUT;
  assign RAM_IMPUT_DATA = OUTPUT_C;

  // Other names for the same wires on the sheet: DIR[3:0] = out_8[3:0]

  // Notes on the sheet:
  //   OPCODE
endmodule

module PC (
  input  [3:0] SET_4BITS,
  input  JUMP_ENABLE,
  input  CLK,
  output [3:0] OUT_PC
);

  wire multiplexer_1_out, not_1_out;

  not not_1 (not_1_out, CLK);
  Multiplexer multiplexer_1 (.in0(not_1_out), .in1(CLK), .out(multiplexer_1_out), .sel(JUMP_ENABLE));
  ADDER_JUMPER adder_jumper_1 (.clock(multiplexer_1_out), .In_4(SET_4BITS), .Jump(JUMP_ENABLE), .OUT_ADDJUMPER(OUT_PC));
  registro4bits registro4bits_1 (.IN_4(OUT_PC), .CLK(multiplexer_1_out), .ENABLE(1'b1));  // open: R, OUT_4
endmodule

module registro8bits (
  input  [7:0] IN_8,
  input  CLK,
  input  Write_Enable,
  input  READ_ENABLE,
  input  R,
  output [7:0] OUT_8
);

  wire and_1_out;
  wire [7:0] d_ff_8_q;

  and and_1 (and_1_out, CLK, Write_Enable);
  D_Flip_Flop #(.trigger("high")) d_ff_1 (
    .D(IN_8[7]), .clk(and_1_out), .Q(d_ff_8_q[7]), .reset(R));  // open: Qn, preset
  D_Flip_Flop #(.trigger("high")) d_ff_2 (
    .D(IN_8[6]), .clk(and_1_out), .Q(d_ff_8_q[6]), .reset(R));  // open: Qn, preset
  D_Flip_Flop #(.trigger("high")) d_ff_3 (
    .D(IN_8[5]), .clk(and_1_out), .Q(d_ff_8_q[5]), .reset(R));  // open: Qn, preset
  D_Flip_Flop #(.trigger("high")) d_ff_4 (
    .D(IN_8[4]), .clk(and_1_out), .Q(d_ff_8_q[4]), .reset(R));  // open: Qn, preset
  D_Flip_Flop #(.trigger("high")) d_ff_5 (
    .D(IN_8[3]), .clk(and_1_out), .Q(d_ff_8_q[3]), .reset(R));  // open: Qn, preset
  D_Flip_Flop #(.trigger("high")) d_ff_6 (
    .D(IN_8[2]), .clk(and_1_out), .Q(d_ff_8_q[2]), .reset(R));  // open: Qn, preset
  D_Flip_Flop #(.trigger("high")) d_ff_7 (
    .D(IN_8[1]), .clk(and_1_out), .Q(d_ff_8_q[1]), .reset(R));  // open: Qn, preset
  D_Flip_Flop #(.trigger("high")) d_ff_8 (
    .D(IN_8[0]), .clk(and_1_out), .Q(d_ff_8_q[0]), .reset(R));  // open: Qn, preset
  assign OUT_8 = READ_ENABLE ? d_ff_8_q : 8'bz;  // Controlled_Buffer controlled_buffer_1
endmodule

module registro4bits (
  input  [3:0] IN_4,
  input  CLK,
  input  ENABLE,
  input  R,
  output [3:0] OUT_4
);

  wire and_1_out;

  and and_1 (and_1_out, CLK, ENABLE);
  D_Flip_Flop d_ff_1 (.D(IN_4[3]), .clk(and_1_out), .Q(OUT_4[3]), .reset(R));  // open: Qn, preset
  D_Flip_Flop d_ff_2 (.D(IN_4[2]), .clk(and_1_out), .Q(OUT_4[2]), .reset(R));  // open: Qn, preset
  D_Flip_Flop d_ff_3 (.D(IN_4[1]), .clk(and_1_out), .Q(OUT_4[1]), .reset(R));  // open: Qn, preset
  D_Flip_Flop d_ff_4 (.D(IN_4[0]), .clk(and_1_out), .Q(OUT_4[0]), .reset(R));  // open: Qn, preset
endmodule

module Gestor_de_lectura_y_escritura (
  input  CLK,
  input  [3:0] OPCODE,
  output RAM_ENABLER
);

  wire and_1_out, and_2_out, and_3_out, and_4_out, and_5_out, and_6_out, and_7_out, and_8_out, not_1_out,
       not_2_out, not_3_out, not_4_out, not_5_out, or_1_out, or_2_out, or_3_out;

  not not_1 (not_1_out, CLK);
  not not_2 (not_2_out, OPCODE[3]);
  not not_3 (not_3_out, OPCODE[2]);
  not not_4 (not_4_out, OPCODE[1]);
  not not_5 (not_5_out, OPCODE[0]);
  and and_1 (and_1_out, not_2_out, OPCODE[2]);
  and and_2 (and_2_out, CLK, not_2_out);
  or or_1 (or_1_out, not_1_out, and_1_out);
  and and_3 (and_3_out, OPCODE[3], not_3_out);
  and and_4 (and_4_out, not_3_out, not_4_out);
  and and_5 (and_5_out, not_3_out, OPCODE[0]);
  and and_6 (and_6_out, and_2_out, not_3_out);
  and and_7 (and_7_out, OPCODE[1], not_5_out);
  or or_2 (or_2_out, or_1_out, and_3_out);
  or or_3 (or_3_out, and_4_out, and_5_out);
  and and_8 (and_8_out, and_6_out, and_7_out);
  or or_4 (RAM_ENABLER, or_2_out, or_3_out);
endmodule

module sandbox (
  input  in_1,
  input  in_2,
  input  [3:0] in_3,
  output [3:0] out_4
);

  COUNTER_JUMP counter_jump_1 (.clock(in_1), .JUMP(in_2), .IN_4(in_3), .COUNT_OUT(out_4));
endmodule

module ALU (
  input  [7:0] in_1,
  input  [7:0] in_2,
  input  [2:0] in_3,
  output [7:0] Y,
  output out_5,
  output out_6,
  output out_7
);

  ALU_E alu_e_1 (.A(in_1), .B(in_2), .OPCODE(in_3), .Y(Y), .Overflow(out_5), .Zero(out_6), .Negative(out_7));
endmodule

// VHDL entity ADDER_JUMPER, as the project stores it:
--------------------------------------------------------------------------------
-- Project :
-- File    :
-- Autor   :
-- Date    :
--
--------------------------------------------------------------------------------
-- Description :
--
--------------------------------------------------------------------------------
LIBRARY ieee;
USE ieee.std_logic_1164.all;
USE ieee.numeric_std.all;

ENTITY ADDER_JUMPER IS
  PORT (
    clock          : IN  std_logic;
    In_4           : IN  std_logic_vector(3 DOWNTO 0);
    Jump           : IN  std_logic;
    OUT_ADDJUMPER  : OUT std_logic_vector(3 DOWNTO 0)
  );
END ADDER_JUMPER;

ARCHITECTURE TypeArchitecture OF ADDER_JUMPER IS

SIGNAL PC : unsigned(3 DOWNTO 0) := "0000";

BEGIN

PROCESS(clock)
BEGIN
    IF rising_edge(clock) THEN
        IF Jump = '1' THEN
            PC <= unsigned(In_4)-1;
        ELSE
            PC <= PC + 1;
        END IF;
    END IF;
END PROCESS;

OUT_ADDJUMPER <= std_logic_vector(PC);

END TypeArchitecture;

// VHDL entity JUMPER, as the project stores it:
library IEEE;
use IEEE.STD_LOGIC_1164.ALL;
use IEEE.NUMERIC_STD.ALL;

entity JUMPER is
    Port (
        Cin   : in  STD_LOGIC_VECTOR(7 downto 0);
        OPCODE : in  STD_LOGIC_VECTOR(3 downto 0);
        Enable : out STD_LOGIC
    );
end JUMPER;

architecture BACK of JUMPER is
begin                                  
    process(OPCODE, Cin)
    	variable temp_Cin : integer;
    	
    begin
    temp_Cin := to_integer(unsigned(Cin));
    
        case OPCODE is
            when "1011" =>              -- ✔️ when correcto dentro del case
                if (temp_Cin > 0 or OPCODE = "1011") then
                    Enable <= '1';
                else                    -- ✔️ else en lugar de segundo if redundante
                    Enable <= '0';      -- ✔️ comillas simples para STD_LOGIC
                end if;   
                
             when "1100" =>
             	if(temp_Cin = 0) then
             		Enable <= '1';
             	else 
             		Enable <= '0';
             	end if;	
            when others =>
                Enable <= '0';          -- ✔️ punto y coma faltaba
        end case;
    end process;
end BACK;

// VHDL entity DECO, as the project stores it:
library IEEE;
use IEEE.STD_LOGIC_1164.ALL;
use IEEE.NUMERIC_STD.ALL;

entity DECO is
    Port (
        ENABLE      : in  STD_LOGIC;
        OPCODE_RAM  : in  STD_LOGIC_VECTOR(3 downto 0);
        C_WRITE     : out STD_LOGIC;
        OPCODE_ALU  : out STD_LOGIC_VECTOR(2 downto 0)
    );
end DECO;

architecture BACK of DECO is
begin                                  
    process(OPCODE_RAM, ENABLE)
    begin
        if ENABLE = '1' then
            case OPCODE_RAM is
                when "0011" =>
                    OPCODE_ALU <= "000";
                    C_WRITE <= '1';
                    
                when "0100" =>
                    OPCODE_ALU <= "001";
                    C_WRITE <= '1';
                    
                when "0101" =>
                    OPCODE_ALU <= "010";
                    C_WRITE <= '1';
                    
                when "0111" =>
                    OPCODE_ALU <= "011";
                    C_WRITE <= '1';

                when "1000" =>
                    OPCODE_ALU <= "100";
                    C_WRITE <= '1';
                    
                when "1001" =>
                    OPCODE_ALU <= "101";
                    C_WRITE <= '1';

                when "1010" =>
                    OPCODE_ALU <= "110";
                    C_WRITE <= '1';
                    
                when "0110" =>
                    OPCODE_ALU <= "111";
                    C_WRITE <= '1';

                when others =>
                    OPCODE_ALU <= "000";
                    C_WRITE <= '0';
            end case;
        else
            OPCODE_ALU <= "000";
            C_WRITE <= '0';
        end if;
    end process;
end BACK;

// VHDL entity COUNTER_JUMP, as the project stores it:
LIBRARY ieee;
USE ieee.std_logic_1164.all;
USE ieee.numeric_std.all;

ENTITY COUNTER_JUMP IS
    PORT (
        clock         : IN  std_logic;
        JUMP          : IN  std_logic;
        IN_4          : IN  std_logic_vector(3 DOWNTO 0);
        COUNT_OUT     : OUT std_logic_vector(3 DOWNTO 0)
    );
END COUNTER_JUMP;

ARCHITECTURE Behavioral OF COUNTER_JUMP IS

    SIGNAL PC         : unsigned(3 DOWNTO 0) := "0000";
    SIGNAL LOAD_NEXT  : std_logic := '0';
    SIGNAL JUMP_VALUE : unsigned(3 DOWNTO 0) := "0000";

BEGIN
    PROCESS(clock)
    BEGIN
        IF rising_edge(clock) THEN
            IF JUMP = '1' THEN
                LOAD_NEXT  <= '1';
                JUMP_VALUE <= unsigned(IN_4);
            ELSE
                LOAD_NEXT  <= '0';
            END IF;
        END IF;
    END PROCESS;

    PROCESS(clock)
    BEGIN
        IF falling_edge(clock) THEN
            IF LOAD_NEXT = '1' THEN
                PC <= JUMP_VALUE;
            ELSE
                IF PC = 15 THEN
                    PC <= "0000";
                ELSE
                    PC <= PC + 1;
                END IF;
            END IF;
        END IF;
    END PROCESS;

COUNT_OUT <= std_logic_vector(PC);

END Behavioral;

// VHDL entity ALU_E, as the project stores it:
library IEEE;
use IEEE.STD_LOGIC_1164.ALL;
use IEEE.NUMERIC_STD.ALL;

entity ALU_E is
    Port (
        A       : in  STD_LOGIC_VECTOR(7 downto 0);
        B       : in  STD_LOGIC_VECTOR(7 downto 0);
        OPCODE  : in  STD_LOGIC_VECTOR(2 downto 0);
        Y       : out STD_LOGIC_VECTOR(7 downto 0);
        Overflow  : out STD_LOGIC;
        Zero      : out STD_LOGIC;
        Negative  : out STD_LOGIC
    );
end ALU_E;

architecture pepe of ALU_E is
    signal op_A : integer;
    signal op_B : integer;
    signal result : integer;
    signal flag_Z : integer;
begin
    process(A, B, OPCODE)
    begin

        Y        <= (others => '0');
        Overflow <= '0';
        Zero     <= '0';
        Negative <= '0';
        op_A <= to_integer(unsigned(A));
        op_B <= to_integer(unsigned(B));
        result <= 0;
        flag_Z <= 0;

        case OPCODE is
            when "011" =>
                Y <= A and B;

            when "100" =>
                Y <= A or B;

            when "110" =>
                Y <= not A;

            when "101" =>
                Y <= A xor B;

            when "000" =>
                if ((unsigned(A) + unsigned(B)) < 256) then
                    Y <= std_logic_vector(unsigned(A) + unsigned(B));
                else
                    Overflow <= '1';
                end if;

            when "001" =>
                if (unsigned(A) - unsigned(B) >= 0 and unsigned(A) >= unsigned(B)) then
                    Y <= std_logic_vector(unsigned(A) - unsigned(B));
                else
                    Negative <= '1';
                    Y <= std_logic_vector(unsigned(A) - unsigned(B));
                end if;

            when "010" =>
                if ((op_A * op_B) < 256) then
                    result <= op_A * op_B;
                    Y <= std_logic_vector(to_unsigned(result, 8));
                else
                    Overflow <= '1';
                end if;

            when "111" =>
                if (op_B /= 0) then
                    result <= op_A / op_B;
                    Y <= std_logic_vector(to_unsigned(result, 8));
                else
                    if (op_B /= 0) then
                        Zero <= '0';
                    end if;
                    if (op_B = 0) then
                        flag_Z <= 1;
                        Zero <= '1';
                    end if;
                end if;

            when others =>
                Y <= (others => '0');
        end case;
    end process;
end pepe;

// VHDL entity ControlUnit, as the project stores it:
library IEEE;
use IEEE.STD_LOGIC_1164.ALL;
use IEEE.NUMERIC_STD.ALL;

entity ControlUnit is
    Port (
        CLK            : in  STD_LOGIC;
        OPCODE         : in  STD_LOGIC_VECTOR(3 downto 0);
        C_IN           : in  STD_LOGIC_VECTOR(7 downto 0);
        A_WRITE_ENABLE : out STD_LOGIC;
        B_WRITE_ENABLE : out STD_LOGIC;
        C_WRITE_ENABLE : out STD_LOGIC;
        C_READ_ENABLE  : out STD_LOGIC;
        C_OUT          : out STD_LOGIC_VECTOR(7 downto 0);
        A_READ         : out STD_LOGIC;
        B_READ         : out STD_LOGIC;
        HALT_ENABLE    : out STD_LOGIC;
        JUMP_ENABLE    : out STD_LOGIC;
        ALU_OPCODE     : out STD_LOGIC_VECTOR(2 downto 0)
    );
end ControlUnit;

architecture TypeArchitecture of ControlUnit is

    SIGNAL HALT_FLAG : STD_LOGIC := '0';

begin

    HALT_LATCH: PROCESS(OPCODE, HALT_FLAG)
    BEGIN
        IF OPCODE = "1111" THEN
            HALT_FLAG <= '1';
        ELSE
            HALT_FLAG <= HALT_FLAG;  -- retiene su valor (latch intencional)
        END IF;
    END PROCESS;

    HALT_ENABLE <= HALT_FLAG;

    PROCESS(CLK, OPCODE, C_IN)
    BEGIN

        A_WRITE_ENABLE <= '0';
        B_WRITE_ENABLE <= '0';
        C_WRITE_ENABLE <= '0';
        C_READ_ENABLE  <= '0';
        C_OUT          <= (OTHERS => '0');
        A_READ         <= '0';
        B_READ         <= '0';
        JUMP_ENABLE    <= '0';
        ALU_OPCODE     <= (OTHERS => '0');
        -- HALT_ENABLE ya no se maneja aquí

        IF CLK = '1' THEN

            CASE OPCODE IS

                -- LOAD A, [Dir]
                WHEN "0000" =>
                    A_WRITE_ENABLE <= '1';

                -- LOAD B, [Dir]
                WHEN "0001" =>
                    B_WRITE_ENABLE <= '1';

                -- STORE C, [Dir]
                WHEN "0010" =>
                    C_READ_ENABLE  <= '1';
                    C_OUT          <= C_IN;

                -- ADD (A + B -> C)
                WHEN "0011" =>
                    A_READ         <= '1';
                    B_READ         <= '1';
                    C_WRITE_ENABLE <= '1';
                    ALU_OPCODE     <= "000";

                -- SUB (A - B -> C)
                WHEN "0100" =>
                    A_READ         <= '1';
                    B_READ         <= '1';
                    C_WRITE_ENABLE <= '1';
                    ALU_OPCODE     <= "001";

                -- MUL (A * B -> C)
                WHEN "0101" =>
                    A_READ         <= '1';
                    B_READ         <= '1';
                    C_WRITE_ENABLE <= '1';
                    ALU_OPCODE     <= "010";

                -- DIV (A / B -> C)
                WHEN "0110" =>
                    A_READ         <= '1';
                    B_READ         <= '1';
                    C_WRITE_ENABLE <= '1';
                    ALU_OPCODE     <= "111";

                -- AND (A AND B -> C)
                WHEN "0111" =>
                    A_READ         <= '1';
                    B_READ         <= '1';
                    C_WRITE_ENABLE <= '1';
                    ALU_OPCODE     <= "011";

                -- OR (A OR B -> C)
                WHEN "1000" =>
                    A_READ         <= '1';
                    B_READ         <= '1';
                    C_WRITE_ENABLE <= '1';
                    ALU_OPCODE     <= "100";

                -- XOR (A XOR B -> C)
                WHEN "1001" =>
                    A_READ         <= '1';
                    B_READ         <= '1';
                    C_WRITE_ENABLE <= '1';
                    ALU_OPCODE     <= "101";

                -- NOT A (NOT A -> C)
                WHEN "1010" =>
                    A_READ         <= '1';
                    C_WRITE_ENABLE <= '1';
                    ALU_OPCODE     <= "110";

                -- JMP [Dir]
                WHEN "1011" =>
                    C_READ_ENABLE  <= '1';
                    JUMP_ENABLE    <= '1';

                -- JZ [Dir]
                WHEN "1100" =>
                    C_READ_ENABLE  <= '1';
                    IF C_IN = "00000000" THEN
                        JUMP_ENABLE <= '1';
                    ELSE
                        JUMP_ENABLE <= '0';
                    END IF;

                WHEN OTHERS =>
                    NULL;

            END CASE;

        END IF;
    END PROCESS;

END TypeArchitecture;

// VHDL entity ram_enabler, as the project stores it:
library IEEE;
use IEEE.STD_LOGIC_1164.ALL;

entity ram_enabler is
    Port ( 
        clk    : in  STD_LOGIC;                         -- Reloj
        opcode : in  STD_LOGIC_VECTOR (3 downto 0);     -- Opcode de 4 bits
        salida : out STD_LOGIC                          -- Señal de salida
    );
end ram_enabler;

architecture Behavioral of ram_enabler is
begin
    -- Lógica combinacional pura:
    -- La salida es 1 solo si el reloj está en nivel alto Y el opcode es "0010"
    -- Si el reloj es '0', la salida es '0' automáticamente.
    
    salida <= '1' when (clk = '1' and opcode = "0010") else '0';
end Behavioral;
