// Logisim project Proyecto_final.circ as structural Verilog
module main (
);

  UC uc_1 ();  // open: A_IN, B_IN, C_IN, RAM_OUTPUT, CLK, ALU_A, ALU_B, RAM_ADDRESS, RAM_IN, A_ENABLE, B_ENABLE, STORE_ENABLE, C_LOAD, ALU_OPCODE, C_ENABLE
endmodule

module registro8bits (
  input  [7:0] IN_8,
  input  CLK,
  input  ENABLE,
  input  R,
  output [7:0] OUT_8
);

  wire and_1_out;

  and and_1 (and_1_out, CLK, ENABLE);
  D_Flip_Flop d_ff_1 (.D(IN_8[7]), .clk(and_1_out), .Q(OUT_8[7]), .reset(R));  // open: Qn, preset
  D_Flip_Flop d_ff_2 (.D(IN_8[6]), .clk(and_1_out), .Q(OUT_8[6]), .reset(R));  // open: Qn, preset
  D_Flip_Flop d_ff_3 (.D(IN_8[5]), .clk(and_1_out), .Q(OUT_8[5]), .reset(R));  // open: Qn, preset
  D_Flip_Flop d_ff_4 (.D(IN_8[4]), .clk(and_1_out), .Q(OUT_8[4]), .reset(R));  // open: Qn, preset
  D_Flip_Flop d_ff_5 (.D(IN_8[3]), .clk(and_1_out), .Q(OUT_8[3]), .reset(R));  // open: Qn, preset
  D_Flip_Flop d_ff_6 (.D(IN_8[2]), .clk(and_1_out), .Q(OUT_8[2]), .reset(R));  // open: Qn, preset
  D_Flip_Flop d_ff_7 (.D(IN_8[1]), .clk(and_1_out), .Q(OUT_8[1]), .reset(R));  // open: Qn, preset
  D_Flip_Flop d_ff_8 (.D(IN_8[0]), .clk(and_1_out), .Q(OUT_8[0]), .reset(R));  // open: Qn, preset
endmodule

module registro4bits (
  input  [3:0] IN_4,
  input  CLK,
  input  ENABLE,
  input  R,
  output [3:0] OUT_4
);

  wire and_1_out;

  and and_1 (and_1_out, CLK, ENABLE);
  D_Flip_Flop d_ff_1 (.D(IN_4[3]), .clk(and_1_out), .Q(OUT_4[3]), .reset(R));  // open: Qn, preset
  D_Flip_Flop d_ff_2 (.D(IN_4[2]), .clk(and_1_out), .Q(OUT_4[2]), .reset(R));  // open: Qn, preset
  D_Flip_Flop d_ff_3 (.D(IN_4[1]), .clk(and_1_out), .Q(OUT_4[1]), .reset(R));  // open: Qn, preset
  D_Flip_Flop d_ff_4 (.D(IN_4[0]), .clk(and_1_out), .Q(OUT_4[0]), .reset(R));  // open: Qn, preset
endmodule

module PC (
  input  [3:0] SET_4BITS,
  input  JUMP_ENABLE,
  input  CLK,
  output [3:0] OUT_PC
);

  wire [3:0] adder_jumper_1_out_addjumper;

  ADDER_JUMPER adder_jumper_1 (
    .clock(CLK), .In_4(SET_4BITS), .Jump(JUMP_ENABLE), .OUT_ADDJUMPER(adder_jumper_1_out_addjumper));
  registro4bits registro4bits_1 (
    .IN_4(adder_jumper_1_out_addjumper), .CLK(CLK), .ENABLE(1'b1), .OUT_4(OUT_PC));  // open: R
endmodule

module UC (
  input  [7:0] RAM_OUTPUT,
  input  [7:0] A_IN,
  input  [7:0] B_IN,
  input  [7:0] C_IN,
  input  CLK,
  output [3:0] RAM_IN,
  output C_ENABLE,
  output [2:0] ALU_OPCODE,
  output A_ENABLE,
  output B_ENABLE,
  output [7:0] ALU_A,
  output STORE_ENABLE,
  output [7:0] ALU_B,
  output [7:0] C_LOAD,
  output [3:0] RAM_ADDRESS
);

  wire and_1_out, controlled_buffer_1_out, jumper_1_enable, not_1_out;
  wire [3:0] registro4bits_2_out_4;
  wire [7:0] registro8bits_1_out_8;

  assign controlled_buffer_1_out = not_1_out ? CLK : 1'bz;  // Controlled_Buffer controlled_buffer_1
  registro8bits registro8bits_1 (
    .IN_8(RAM_OUTPUT), .CLK(controlled_buffer_1_out), .ENABLE(controlled_buffer_1_out),
    .OUT_8(registro8bits_1_out_8));  // open: R
  not not_1 (not_1_out, and_1_out);
  PC pc_1 (.SET_4BITS(RAM_IN), .JUMP_ENABLE(jumper_1_enable), .CLK(controlled_buffer_1_out), .OUT_PC(RAM_ADDRESS));
  and and_1 (and_1_out, registro4bits_2_out_4[0], registro4bits_2_out_4[1], registro4bits_2_out_4[2], registro4bits_2_out_4[3]);
  registro4bits registro4bits_1 (
    .IN_4(registro8bits_1_out_8[3:0]), .CLK(controlled_buffer_1_out), .ENABLE(controlled_buffer_1_out),
    .OUT_4(RAM_IN));  // open: R
  registro4bits registro4bits_2 (
    .IN_4(registro8bits_1_out_8[7:4]), .CLK(controlled_buffer_1_out), .ENABLE(controlled_buffer_1_out),
    .OUT_4(registro4bits_2_out_4));  // open: R
  LOADERS loaders_1 (
    .OPCODE(registro4bits_2_out_4), .C_IN(C_IN), .A_WRITE_ENABLE(A_ENABLE), .B_WRITE_ENABLE(B_ENABLE),
    .C_STORE_ENABLE(STORE_ENABLE), .C_OUT(C_LOAD));
  JUMPER jumper_1 (.Cin(C_IN), .OPCODE(registro4bits_2_out_4), .Enable(jumper_1_enable));
  DECO deco_1 (.OPCODE_RAM(registro4bits_2_out_4), .C_WRITE(C_ENABLE), .OPCODE_ALU(ALU_OPCODE));

  assign ALU_A = A_IN;
  assign ALU_B = B_IN;

  // Notes on the sheet:
  //   OPCODE
endmodule

module SANDBOX (
  input  [3:0] in_1,
  input  [3:0] in_2,
  input  [7:0] in_3,
  input  [7:0] in_4,
  input  [3:0] in_5,
  output out_6,
  output out_7,
  output out_8,
  output out_9,
  output [2:0] out_10,
  output [7:0] out_11,
  output out_12
);

  LOADERS loaders_1 (
    .OPCODE(in_1), .C_IN(in_3), .A_WRITE_ENABLE(out_6), .B_WRITE_ENABLE(out_8), .C_STORE_ENABLE(out_9),
    .C_OUT(out_11));
  JUMPER jumper_1 (.Cin(in_4), .OPCODE(in_5), .Enable(out_12));
  DECO deco_1 (.OPCODE_RAM(in_2), .C_WRITE(out_7), .OPCODE_ALU(out_10));
endmodule

// VHDL entity ADDER_JUMPER, as the project stores it:
--------------------------------------------------------------------------------
-- Project :
-- File    :
-- Autor   :
-- Date    :
--
--------------------------------------------------------------------------------
-- Description :
--
--------------------------------------------------------------------------------
LIBRARY ieee;
USE ieee.std_logic_1164.all;
USE ieee.numeric_std.all;

ENTITY ADDER_JUMPER IS
  PORT (
    clock          : IN  std_logic;
    In_4           : IN  std_logic_vector(3 DOWNTO 0);
    Jump           : IN  std_logic;
    OUT_ADDJUMPER  : OUT std_logic_vector(3 DOWNTO 0)
  );
END ADDER_JUMPER;

ARCHITECTURE TypeArchitecture OF ADDER_JUMPER IS

SIGNAL PC : unsigned(3 DOWNTO 0) := "0000";

BEGIN

PROCESS(clock)
BEGIN
    IF rising_edge(clock) THEN
        IF Jump = '1' THEN
            PC <= unsigned(In_4);
        ELSE
            PC <= PC + 1;
        END IF;
    END IF;
END PROCESS;

OUT_ADDJUMPER <= std_logic_vector(PC);

END TypeArchitecture;

// VHDL entity LOADERS, as the project stores it:
--------------------------------------------------------------------------------
-- Project :
-- File    :
-- Autor   :
-- Date    :
--
--------------------------------------------------------------------------------
-- Description :
--
--------------------------------------------------------------------------------

LIBRARY ieee;
USE ieee.std_logic_1164.all;

ENTITY LOADERS IS
  PORT (
  ------------------------------------------------------------------------------
  --Insert input ports below
    OPCODE     : IN  std_logic_vector(3 DOWNTO 0);                    -- input bit example
    C_IN        : IN  std_logic_vector(7 DOWNTO 0); -- input vector example
  ------------------------------------------------------------------------------
  --Insert output ports below
    A_WRITE_ENABLE        : OUT std_logic;                    -- output bit example
    B_WRITE_ENABLE        : OUT std_logic;
    C_STORE_ENABLE        : OUT std_logic;
    C_OUT        : OUT  std_logic_vector(7 DOWNTO 0)-- output vector example
    );
END LOADERS;



ARCHITECTURE TypeArchitecture OF LOADERS IS

BEGIN
PROCESS(OPCODE, C_IN)
BEGIN
    A_WRITE_ENABLE <= '0';
    B_WRITE_ENABLE <= '0';
    C_STORE_ENABLE <= '0';
    C_OUT          <= (OTHERS => '0');

    CASE OPCODE IS

        WHEN "0000" =>              
            A_WRITE_ENABLE <= '1';

        WHEN "0001" =>           
            B_WRITE_ENABLE <= '1';

        WHEN "0010" =>             
            C_STORE_ENABLE <= '1';
            C_OUT          <= C_IN;

        WHEN OTHERS =>             
            NULL;

    END CASE;
END PROCESS;
END TypeArchitecture;

// VHDL entity JUMPER, as the project stores it:
library IEEE;
use IEEE.STD_LOGIC_1164.ALL;
use IEEE.NUMERIC_STD.ALL;

entity JUMPER is
    Port (
        Cin   : in  STD_LOGIC_VECTOR(7 downto 0);
        OPCODE : in  STD_LOGIC_VECTOR(3 downto 0);
        Enable : out STD_LOGIC
    );
end JUMPER;

architecture BACK of JUMPER is
begin                                  
    process(OPCODE, Cin)
    	variable temp_Cin : integer;
    	
    begin
    temp_Cin := to_integer(unsigned(Cin));
    
        case OPCODE is
            when "1011" =>              -- ✔️ when correcto dentro del case
                if (temp_Cin > 0 or OPCODE = "1011") then
                    Enable <= '1';
                else                    -- ✔️ else en lugar de segundo if redundante
                    Enable <= '0';      -- ✔️ comillas simples para STD_LOGIC
                end if;   
                
             when "1100" =>
             	if(temp_Cin = 0) then
             		Enable <= '1';
             	else 
             		Enable <= '0';
             	end if;	
            when others =>
                Enable <= '0';          -- ✔️ punto y coma faltaba
        end case;
    end process;
end BACK;

// VHDL entity DECO, as the project stores it:
library IEEE;
use IEEE.STD_LOGIC_1164.ALL;
use IEEE.NUMERIC_STD.ALL;

entity DECO is
    Port (
    
        OPCODE_RAM   : in  STD_LOGIC_VECTOR(3 downto 0);
        C_WRITE : out std_logic;
        OPCODE_ALU : out STD_LOGIC_VECTOR(2 downto 0)
    );
end DECO ;

architecture BACK of DECO is
begin                                  
    process(OPCODE_RAM)
    begin
        case OPCODE_RAM is
            when "0011" =>             
			OPCODE_ALU <= "000";
			C_WRITE <= '1';
                
             when "0100" =>
             	OPCODE_ALU <= "001";
             	C_WRITE <= '1';
             	
             when "0101" =>             
			OPCODE_ALU <= "010";
			C_WRITE <= '1';
                
             when "0111" =>
             	OPCODE_ALU <= "011";
             	C_WRITE <= '1';

        	   when "1000" =>             
			OPCODE_ALU <= "100";
			C_WRITE <= '1';
                
             when "1001" =>
             	OPCODE_ALU <= "101";
             	C_WRITE <= '1';

             when "1010" =>             
			OPCODE_ALU <= "110";
			C_WRITE <= '1';
                
             when "0110" =>
             	OPCODE_ALU <= "111";
             	C_WRITE <= '1';

             
            when others =>
                
                C_WRITE <= '0';
        end case;
    end process;
end BACK;
