// Logisim project modificaciones_mayores_de_PC.circ as structural Verilog
module main (
);

  UC uc_1 ();  // open: Reloj, OUTPUT_C, ALU_OUTPUT, RAM_OUTPUT, INPUT_B, INPUT_A, out_7, out_19, RAM_IMPUT_ADDRESS, READ_ENABLE, WRITE_ENABLE, A_READ, B_READ, A_write, B_write, C_READ, RAM_IMPUT_DATA, C_Write, OP_CODEALU, INPUT_C
endmodule

module registro8bits (
  input  [7:0] IN_8,
  input  CLK,
  input  Write_Enable,
  input  READ_ENABLE,
  input  R,
  output [7:0] OUT_8
);

  wire and_1_out;
  wire [7:0] d_ff_8_q;

  and and_1 (and_1_out, CLK, Write_Enable);
  D_Flip_Flop d_ff_1 (.D(IN_8[7]), .clk(and_1_out), .Q(d_ff_8_q[7]), .reset(R));  // open: Qn, preset
  D_Flip_Flop d_ff_2 (.D(IN_8[6]), .clk(and_1_out), .Q(d_ff_8_q[6]), .reset(R));  // open: Qn, preset
  D_Flip_Flop d_ff_3 (.D(IN_8[5]), .clk(and_1_out), .Q(d_ff_8_q[5]), .reset(R));  // open: Qn, preset
  D_Flip_Flop d_ff_4 (.D(IN_8[4]), .clk(and_1_out), .Q(d_ff_8_q[4]), .reset(R));  // open: Qn, preset
  D_Flip_Flop d_ff_5 (.D(IN_8[3]), .clk(and_1_out), .Q(d_ff_8_q[3]), .reset(R));  // open: Qn, preset
  D_Flip_Flop d_ff_6 (.D(IN_8[2]), .clk(and_1_out), .Q(d_ff_8_q[2]), .reset(R));  // open: Qn, preset
  D_Flip_Flop d_ff_7 (.D(IN_8[1]), .clk(and_1_out), .Q(d_ff_8_q[1]), .reset(R));  // open: Qn, preset
  D_Flip_Flop d_ff_8 (.D(IN_8[0]), .clk(and_1_out), .Q(d_ff_8_q[0]), .reset(R));  // open: Qn, preset
  assign OUT_8 = READ_ENABLE ? d_ff_8_q : 8'bz;  // Controlled_Buffer controlled_buffer_1
endmodule

module registro4bits (
  input  [3:0] IN_4,
  input  CLK,
  input  ENABLE,
  input  R,
  output [3:0] OUT_4
);

  wire and_1_out;

  and and_1 (and_1_out, CLK, ENABLE);
  D_Flip_Flop d_ff_1 (.D(IN_4[3]), .clk(and_1_out), .Q(OUT_4[3]), .reset(R));  // open: Qn, preset
  D_Flip_Flop d_ff_2 (.D(IN_4[2]), .clk(and_1_out), .Q(OUT_4[2]), .reset(R));  // open: Qn, preset
  D_Flip_Flop d_ff_3 (.D(IN_4[1]), .clk(and_1_out), .Q(OUT_4[1]), .reset(R));  // open: Qn, preset
  D_Flip_Flop d_ff_4 (.D(IN_4[0]), .clk(and_1_out), .Q(OUT_4[0]), .reset(R));  // open: Qn, preset
endmodule

module PC (
  input  [3:0] SET_4BITS,
  input  JUMP_ENABLE,
  input  CLK,
  output [3:0] OUT_PC
);

  wire multiplexer_1_out, not_1_out;

  not not_1 (not_1_out, CLK);
  Multiplexer multiplexer_1 (.in0(not_1_out), .in1(CLK), .out(multiplexer_1_out), .sel(JUMP_ENABLE));
  ADDER_JUMPER adder_jumper_1 (.clock(multiplexer_1_out), .In_4(SET_4BITS), .Jump(JUMP_ENABLE), .OUT_ADDJUMPER(OUT_PC));
  registro4bits registro4bits_1 (.IN_4(OUT_PC), .CLK(multiplexer_1_out), .ENABLE(1'b1));  // open: R, OUT_4
endmodule

module UC (
  input  [7:0] RAM_OUTPUT,
  input  [7:0] ALU_OUTPUT,
  input  [7:0] OUTPUT_C,
  input  Reloj,
  output [7:0] INPUT_B,
  output [7:0] INPUT_A,
  output [7:0] out_7,
  output [7:0] INPUT_C,
  output A_write,
  output B_write,
  output C_READ,
  output [7:0] RAM_IMPUT_DATA,
  output C_Write,
  output A_READ,
  output B_READ,
  output [2:0] OP_CODEALU,
  output READ_ENABLE,
  output WRITE_ENABLE,
  output [3:0] out_19,
  output [3:0] RAM_IMPUT_ADDRESS
);

  wire and_1_out, enabler_process_1_loaders, Execute_enable, jumper_1_enable,
       loadersanddir_enable_1_dir_enable, not_1_out, not_2_out;
  wire [3:0] undriven;

  not not_1 (not_1_out, Reloj);
  not not_2 (not_2_out, Reloj);
  registro8bits registro8bits_1 (
    .IN_8(RAM_OUTPUT), .CLK(not_1_out), .Write_Enable(not_2_out), .READ_ENABLE(Reloj), .OUT_8(out_7));  // open: R
  COUNTER_JUMP counter_jump_1 (.clock(Reloj), .JUMP(jumper_1_enable), .IN_4(out_7[3:0]), .COUNT_OUT(out_19));
  // NOT_Gate not_3 has open pins: in=and_1_out, out=open
  and and_1 (and_1_out, undriven[0], undriven[1], undriven[2], undriven[3]);
  Multiplexer #(.width(4)) multiplexer_1 (
    .in0(out_19), .in1(out_7[3:0]), .out(RAM_IMPUT_ADDRESS), .sel(Execute_enable));
  and and_2 (Execute_enable, loadersanddir_enable_1_dir_enable, Reloj);
  Gestor_de_lectura_y_escritura gestor_de_lectura_y_escritura_1 (
    .CLK(Reloj), .OPCODE(out_7[7:4]), .READ_RAM(READ_ENABLE), .WRITE_RAM(WRITE_ENABLE));
  ENABLER_Process enabler_process_1 (.IN_4(out_7[7:4]), .loaders(enabler_process_1_loaders), .Alu(A_READ));
  LOADERSANDDIR_ENABLE loadersanddir_enable_1 (
    .LOAD_ENABLE(enabler_process_1_loaders), .OPCODE(out_7[7:4]), .C_IN(OUTPUT_C), .A_WRITE_ENABLE(A_write),
    .B_WRITE_ENABLE(B_write), .C_READ_ENABLE(C_READ), .C_OUT(RAM_IMPUT_DATA),
    .DIR_ENABLE(loadersanddir_enable_1_dir_enable));
  JUMPER jumper_1 (.Cin(RAM_IMPUT_DATA), .OPCODE(out_7[7:4]), .Enable(jumper_1_enable));
  DECO deco_1 (.ENABLE(A_READ), .OPCODE_RAM(out_7[7:4]), .C_WRITE(C_Write), .OPCODE_ALU(OP_CODEALU));

  assign B_READ = A_READ;
  assign INPUT_A = RAM_OUTPUT;
  assign INPUT_B = RAM_OUTPUT;
  assign INPUT_C = ALU_OUTPUT;

  // Other names for the same wires on the sheet: DIR[3:0] = out_7[3:0]; Reloj_gestor = Reloj

  // Notes on the sheet:
  //   OPCODE
endmodule

module ENABLER_Process (
  input  [3:0] IN_4,
  output loaders,
  output Alu
);

  wire and_1_out, and_2_out, and_3_out, and_4_out, and_5_out, and_6_out, and_7_out, and_8_out, not_1_out,
       not_2_out, not_3_out, not_4_out;

  not not_1 (not_1_out, IN_4[3]);
  not not_2 (not_2_out, IN_4[2]);
  not not_3 (not_3_out, IN_4[1]);
  not not_4 (not_4_out, IN_4[0]);
  and and_1 (and_1_out, not_1_out, not_2_out, not_3_out);
  and and_2 (and_2_out, not_1_out, not_2_out, not_4_out);
  and and_3 (and_3_out, IN_4[3], not_2_out, IN_4[1], IN_4[0]);
  and and_4 (and_4_out, IN_4[3], IN_4[2], not_3_out, not_4_out);
  and and_5 (and_5_out, not_1_out, IN_4[1], IN_4[0]);
  and and_6 (and_6_out, not_1_out, IN_4[2]);
  and and_7 (and_7_out, IN_4[3], not_2_out, not_3_out);
  and and_8 (and_8_out, IN_4[3], not_2_out, not_4_out);
  or or_1 (loaders, and_1_out, and_2_out, and_3_out, and_4_out);
  or or_2 (Alu, and_5_out, and_6_out, and_7_out, and_8_out);
endmodule

module Gestor_de_lectura_y_escritura (
  input  CLK,
  input  [3:0] OPCODE,
  output READ_RAM,
  output WRITE_RAM
);

  wire and_1_out, and_2_out, and_3_out, and_4_out, and_5_out, and_6_out, not_1_out, not_2_out, not_3_out,
       not_4_out, not_5_out, or_1_out, or_2_out, or_3_out;

  not not_1 (not_1_out, CLK);
  not not_2 (not_2_out, OPCODE[3]);
  not not_3 (not_3_out, OPCODE[2]);
  not not_4 (not_4_out, OPCODE[1]);
  not not_5 (not_5_out, OPCODE[0]);
  and and_1 (and_1_out, not_2_out, not_4_out);
  and and_2 (and_2_out, not_2_out, not_3_out);
  and and_3 (and_3_out, OPCODE[1], not_5_out);
  or or_1 (or_1_out, not_1_out, and_1_out);
  and and_4 (and_4_out, OPCODE[3], not_3_out);
  and and_5 (and_5_out, OPCODE[1], OPCODE[0]);
  and and_6 (and_6_out, OPCODE[2], OPCODE[1]);
  and and_7 (WRITE_RAM, and_2_out, and_3_out);
  or or_2 (or_2_out, or_1_out, and_4_out);
  or or_3 (or_3_out, and_5_out, and_6_out);
  or or_4 (READ_RAM, or_2_out, or_3_out);
endmodule

module sandbox (
  input  in_1,
  input  in_2,
  input  [3:0] in_3,
  output [3:0] out_4
);

  COUNTER_JUMP counter_jump_1 (.clock(in_1), .JUMP(in_2), .IN_4(in_3), .COUNT_OUT(out_4));
endmodule

// VHDL entity ADDER_JUMPER, as the project stores it:
--------------------------------------------------------------------------------
-- Project :
-- File    :
-- Autor   :
-- Date    :
--
--------------------------------------------------------------------------------
-- Description :
--
--------------------------------------------------------------------------------
LIBRARY ieee;
USE ieee.std_logic_1164.all;
USE ieee.numeric_std.all;

ENTITY ADDER_JUMPER IS
  PORT (
    clock          : IN  std_logic;
    In_4           : IN  std_logic_vector(3 DOWNTO 0);
    Jump           : IN  std_logic;
    OUT_ADDJUMPER  : OUT std_logic_vector(3 DOWNTO 0)
  );
END ADDER_JUMPER;

ARCHITECTURE TypeArchitecture OF ADDER_JUMPER IS

SIGNAL PC : unsigned(3 DOWNTO 0) := "0000";

BEGIN

PROCESS(clock)
BEGIN
    IF rising_edge(clock) THEN
        IF Jump = '1' THEN
            PC <= unsigned(In_4)-1;
        ELSE
            PC <= PC + 1;
        END IF;
    END IF;
END PROCESS;

OUT_ADDJUMPER <= std_logic_vector(PC);

END TypeArchitecture;

// VHDL entity LOADERSANDDIR_ENABLE, as the project stores it:
LIBRARY ieee;
USE ieee.std_logic_1164.all;

ENTITY LOADERSANDDIR_ENABLE IS
  PORT (
  ----------------------------------------------------------------------------
  --Insert input ports below
    LOAD_ENABLE : IN  std_logic;                      
    OPCODE      : IN  std_logic_vector(3 DOWNTO 0);
    C_IN        : IN  std_logic_vector(7 DOWNTO 0);
  ----------------------------------------------------------------------------
  --Insert output ports below
    A_WRITE_ENABLE : OUT std_logic;
    B_WRITE_ENABLE : OUT std_logic;
    C_READ_ENABLE : OUT std_logic;
    C_OUT          : OUT std_logic_vector(7 DOWNTO 0);
    DIR_ENABLE : OUT std_logic
  );
END LOADERSANDDIR_ENABLE;


ARCHITECTURE TypeArchitecture OF LOADERSANDDIR_ENABLE IS

BEGIN
PROCESS(LOAD_ENABLE, OPCODE, C_IN)
BEGIN
    A_WRITE_ENABLE <= '0';
    B_WRITE_ENABLE <= '0';
    C_READ_ENABLE <= '0';
    C_OUT          <= (OTHERS => '0');
    DIR_ENABLE <= '0';
    IF LOAD_ENABLE = '1' THEN       

        CASE OPCODE IS

            WHEN "0000" =>
                A_WRITE_ENABLE <= '1';
                DIR_ENABLE <= '1';

            WHEN "0001" =>
                B_WRITE_ENABLE <= '1';
                DIR_ENABLE <= '1';

            WHEN "0010" =>
                C_READ_ENABLE <= '1';
                C_OUT          <= C_IN;
                DIR_ENABLE <= '1';
            WHEN "1011" =>
                DIR_ENABLE <= '1';
                C_READ_ENABLE <= '1';

            WHEN "1100" =>
                DIR_ENABLE <= '1';
                C_READ_ENABLE <= '1';


            WHEN OTHERS =>
                NULL;

        END CASE;
		DIR_ENABLE <= '1';
    END IF;
END PROCESS;
END TypeArchitecture;

// VHDL entity JUMPER, as the project stores it:
library IEEE;
use IEEE.STD_LOGIC_1164.ALL;
use IEEE.NUMERIC_STD.ALL;

entity JUMPER is
    Port (
        Cin   : in  STD_LOGIC_VECTOR(7 downto 0);
        OPCODE : in  STD_LOGIC_VECTOR(3 downto 0);
        Enable : out STD_LOGIC
    );
end JUMPER;

architecture BACK of JUMPER is
begin                                  
    process(OPCODE, Cin)
    	variable temp_Cin : integer;
    	
    begin
    temp_Cin := to_integer(unsigned(Cin));
    
        case OPCODE is
            when "1011" =>              -- ✔️ when correcto dentro del case
                if (temp_Cin > 0 or OPCODE = "1011") then
                    Enable <= '1';
                else                    -- ✔️ else en lugar de segundo if redundante
                    Enable <= '0';      -- ✔️ comillas simples para STD_LOGIC
                end if;   
                
             when "1100" =>
             	if(temp_Cin = 0) then
             		Enable <= '1';
             	else 
             		Enable <= '0';
             	end if;	
            when others =>
                Enable <= '0';          -- ✔️ punto y coma faltaba
        end case;
    end process;
end BACK;

// VHDL entity DECO, as the project stores it:
library IEEE;
use IEEE.STD_LOGIC_1164.ALL;
use IEEE.NUMERIC_STD.ALL;

entity DECO is
    Port (
        ENABLE      : in  STD_LOGIC;
        OPCODE_RAM  : in  STD_LOGIC_VECTOR(3 downto 0);
        C_WRITE     : out STD_LOGIC;
        OPCODE_ALU  : out STD_LOGIC_VECTOR(2 downto 0)
    );
end DECO;

architecture BACK of DECO is
begin                                  
    process(OPCODE_RAM, ENABLE)
    begin
        if ENABLE = '1' then
            case OPCODE_RAM is
                when "0011" =>
                    OPCODE_ALU <= "000";
                    C_WRITE <= '1';
                    
                when "0100" =>
                    OPCODE_ALU <= "001";
                    C_WRITE <= '1';
                    
                when "0101" =>
                    OPCODE_ALU <= "010";
                    C_WRITE <= '1';
                    
                when "0111" =>
                    OPCODE_ALU <= "011";
                    C_WRITE <= '1';

                when "1000" =>
                    OPCODE_ALU <= "100";
                    C_WRITE <= '1';
                    
                when "1001" =>
                    OPCODE_ALU <= "101";
                    C_WRITE <= '1';

                when "1010" =>
                    OPCODE_ALU <= "110";
                    C_WRITE <= '1';
                    
                when "0110" =>
                    OPCODE_ALU <= "111";
                    C_WRITE <= '1';

                when others =>
                    OPCODE_ALU <= "000";
                    C_WRITE <= '0';
            end case;
        else
            OPCODE_ALU <= "000";
            C_WRITE <= '0';
        end if;
    end process;
end BACK;

// VHDL entity COUNTER_JUMP, as the project stores it:
LIBRARY ieee;
USE ieee.std_logic_1164.all;
USE ieee.numeric_std.all;

ENTITY COUNTER_JUMP IS
    PORT (
        clock         : IN  std_logic;
        JUMP          : IN  std_logic;
        IN_4          : IN  std_logic_vector(3 DOWNTO 0);
        COUNT_OUT     : OUT std_logic_vector(3 DOWNTO 0)
    );
END COUNTER_JUMP;

ARCHITECTURE Behavioral OF COUNTER_JUMP IS

    SIGNAL PC         : unsigned(3 DOWNTO 0) := "0000";
    SIGNAL LOAD_NEXT  : std_logic := '0';
    SIGNAL JUMP_VALUE : unsigned(3 DOWNTO 0) := "0000";

BEGIN
    PROCESS(clock)
    BEGIN
        IF rising_edge(clock) THEN
            IF JUMP = '1' THEN
                LOAD_NEXT  <= '1';
                JUMP_VALUE <= unsigned(IN_4);
            ELSE
                LOAD_NEXT  <= '0';
            END IF;
        END IF;
    END PROCESS;

    PROCESS(clock)
    BEGIN
        IF falling_edge(clock) THEN
            IF LOAD_NEXT = '1' THEN
                PC <= JUMP_VALUE;
            ELSE
                IF PC = 15 THEN
                    PC <= "0000";
                ELSE
                    PC <= PC + 1;
                END IF;
            END IF;
        END IF;
    END PROCESS;

COUNT_OUT <= std_logic_vector(PC);

END Behavioral;
